# Fritzing sketch Proyecto_1_Paralelo (saved by Fritzing 0.9.3b)
breadboards: 1

parts:
  Componente1 = Arduino Uno (Rev3)
  S1 = Pushbutton [package="[THT]"]
  LED1 = LED - 5mm [color="Red (633nm)" package="5 mm [THT]"]
  R1 = Resistor [tolerance=±5% resistance=220 package=THT]
  S2 = Pushbutton [package="[THT]"]

nets:
  N1: Componente1.GND, R1.Pin_0
  N2: Componente1.5V, S1.Pin_1, S1.Pin_2, S2.Pin_1, S2.Pin_2
  N3: S1.Pin_3, S1.Pin_4, LED1.anode, S2.Pin_3, S2.Pin_4
  N4: LED1.cathode, R1.Pin_1
