# Fritzing sketch interruptor_simple (saved by Fritzing 0.9.3b)
breadboards: 1

parts:
  Componente1 = Arduino Uno (Rev3)
  R1 = Resistor [tolerance=±5% resistance=220 package=THT]
  LED1 = LED - 5mm [color="Red (633nm)" package="5 mm [THT]"]
  S1 = Pushbutton [package="[THT]"]
  R2 = Resistor [tolerance=±5% resistance=10k package=THT]

nets:
  N1: Componente1.GND, Componente1.D3_PWM, R1.Pin_0, S1.Pin_1, S1.Pin_2, S1.Pin_3, S1.Pin_4, R2.Pin_0
  N2: Componente1.D2, LED1.anode
  N3: R1.Pin_1, LED1.cathode
