# Fritzing sketch ProjectoArduino_02_Spaceship Interface Project (saved by Fritzing 0.9.2b)
breadboards: 1

parts:
  LED1 = LED - 5mm [color="Red (633nm)" package="5 mm [THT]"]
  LED2 = LED - 5mm [color="Red (633nm)" package="5 mm [THT]"]
  LED3 = LED - 5mm [color="Red (633nm)" package="5 mm [THT]"]
  R1 = Resistor [tolerance=±5% resistance=220 package=THT]
  R2 = Resistor [tolerance=±5% resistance=220 package=THT]
  R3 = Resistor [tolerance=±5% resistance=220 package=THT]
  Part1 = Arduino Uno (Rev3)
  S1 = Pushbutton [package="[THT]"]
  R4 = Resistor [tolerance=±5% resistance=220 package=THT]

nets:
  N1: LED1.cathode, Part1.D5_PWM
  N2: LED1.anode, R1.Pin_1
  N3: LED2.cathode, Part1.D4
  N4: LED2.anode, R2.Pin_1
  N5: LED3.cathode, Part1.D3_PWM
  N6: LED3.anode, R3.Pin_1
  N7: R1.Pin_0, R2.Pin_0, R3.Pin_0, Part1.GND, R4.Pin_0
  N8: Part1.D2, S1.Pin_1, S1.Pin_2, R4.Pin_1
  N9: Part1.5V, S1.Pin_3, S1.Pin_4
